# Fritzing sketch SIM-FRITZ (saved by Fritzing 0.9.3b)

parts:
  Part1 = Arduino Uno (Rev3)
  SIM1 = SIM808 - GPS/GPRS/GSM [package=SIM]

nets:
  N1: Part1.D8, SIM1.RXD
  N2: Part1.GND, SIM1.LI-ion_-
  N3: Part1.D7, SIM1.TXD

custom parts:
  SIM808 - GPS/GPRS/GSM: Este módulo está basado en el chip SIMCOM SIM808 y nos ofrece, además de las funcionalidades de envío y recepción de datos GSM/GPRS (la de los teléfonos móviles 2g), la tecnología GPS de navegación por satélite. O sea que, gracias a este módulo y utilizando una tarjeta SIM, seremos capaces de enviar y recibir llamadas y SMS, conectarnos a Internet y conocer nuestras coordenadas y el horario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
